# Fritzing sketch ESP8266-01-Fritzing (saved by Fritzing 0.9.1b)
circuit board: 8.46667cm x 5.64444cm
breadboards: 1

parts:
  J1 = double row female pin header, 4 pins [form="♀ (female)"]
  J2 = double row female pin header, 4 pins [form="♀ (female)"]
  R1 = Resistor [tolerance=±5% resistance=1k package=THT]
  R2 = Resistor [tolerance=±5% resistance=1.8k package=THT]
  S1 = Pushbutton [package="[THT]"]
  R3 = Resistor [tolerance=±5% resistance=10k package=THT]
  Part1 = FTDI Basic Programmer
  R7 = Resistor [tolerance=±5% resistance=10k package=THT]

nets:
  N1: J1.pin1, Part1.RXI
  N2: J1.pin2, R7.Pin_1
  N3: J1.pin3, R3.Pin_1
  N4: J1.pin4, R3.Pin_0, Part1.POWER, R7.Pin_0
  N5: J2.pin1, R2.Pin_1, S1.Pin_1, S1.Pin_2, Part1.GND
  N6: J2.pin3, S1.Pin_3, S1.Pin_4
  N7: J2.pin4, R1.Pin_1, R2.Pin_0
  N8: R1.Pin_0, Part1.TXO
